// Logisim project s-mips.circ as structural Verilog: 23 circuits, main circuit S-MIPS Board
module S_MIPS_Board (
  input  DESHABILITAR_DISPATCHER,
  output halt
);

  wire button_1_out, CLK, CS, d_ff_1_q, LCLR, LoadRAM, LoadRAMOn, LW, R_R_W, R_W, ram_dispatcher_1_finished,
       RCS, Reset_out, RST, TTY_EN;
  wire [2:0] KDB;
  wire [3:0] LMask, Mask, ram_1_read_time, ram_1_write_time, RMask;
  wire [6:0] KDB_DATA, TTY_DATA;
  wire [15:0] Addr, LAddr, RAddr;
  wire [31:0] I0, I1, I2, I3, LData, ram_1_data_out_0, ram_1_data_out_1, ram_1_data_out_2, ram_1_data_out_3,
       RI0, RI1, RI2, RI3;

  TTY #(.rows(25), .cols(80)) tty_1 (.data(TTY_DATA), .clk(CLK), .we(TTY_EN), .clr(RST));
  not not_1 (LoadRAMOn, ram_dispatcher_1_finished);
  RAM_Dispatcher ram_dispatcher_1 (
    .WriteTime(ram_1_write_time), .Clock(CLK), .Data(LData), .Address(LAddr), .Mask(LMask),
    .Finished(ram_dispatcher_1_finished), .Write(LW), .CLR(LCLR));
  Keyboard #(.buflen(64)) keyboard_1 (.clk(CLK), .re(KDB[0]), .avail(KDB[2]), .data(KDB_DATA));  // open: clr
  RAM ram_1 (
    .Address(RAddr), .Data_Out_0(ram_1_data_out_0), .Data_Out_1(ram_1_data_out_1),
    .Data_Out_2(ram_1_data_out_2), .Data_Out_3(ram_1_data_out_3), .Data_In_0(RI0), .Data_In_1(RI1),
    .Data_In_2(RI2), .Data_In_3(RI3), .Mask(RMask), .nRead_Write(R_R_W), .Chip_Select(RCS),
    .Read_Time(ram_1_read_time), .Reset(button_1_out), .Write_Time(ram_1_write_time));
  Button button_1 (.out(button_1_out));
  D_Flip_Flop d_ff_1 (.clk(CLK), .D(1'b1), .Q(d_ff_1_q), .reset(Reset_out));  // open: Qn, preset, en
  Button Reset (.out(Reset_out));
  S_MIPS s_mips_1 (
    .Kbd_Enable(KDB[0]), .Address(Addr), .Kbd_Clear(KDB[1]), .Kbd_Available(KDB[2]), .RAM_In_0(I0),
    .Kbd_ASCII_Data(KDB_DATA), .RAM_In_1(I1), .TTY_Enable(TTY_EN), .RAM_In_2(I2), .RAM_In_3(I3),
    .TTY_ASCII_Data(TTY_DATA), .Reset(RST), .RAM_Out_0(ram_1_data_out_0), .Clock(CLK),
    .RAM_Out_1(ram_1_data_out_1), .Stop(halt), .RAM_Out_2(ram_1_data_out_2), .RAM_Out_3(ram_1_data_out_3),
    .Mask(Mask), .Read_Time(ram_1_read_time), .Write_Time(ram_1_write_time), .nRead_Write(R_W),
    .Chip_Select(CS));
  D_Flip_Flop d_ff_2 (.clk(CLK), .D(d_ff_1_q), .Qn(LCLR), .reset(Reset_out));  // open: Q, preset, en
  or or_1 (RST, LCLR, LoadRAM);
  Clock clock_1 (.out(CLK));
  Multiplexer #(.width(32), .enable("false")) multiplexer_1 (.in0(I0), .in1(LData), .out(RI0), .sel(LoadRAM));
  Multiplexer #(.width(32), .enable("false")) multiplexer_2 (.in0(I1), .in1(LData), .out(RI1), .sel(LoadRAM));
  Multiplexer #(.width(32), .enable("false")) multiplexer_3 (.in0(I2), .in1(LData), .out(RI2), .sel(LoadRAM));
  Multiplexer #(.width(32), .enable("false")) multiplexer_4 (.in0(I3), .in1(LData), .out(RI3), .sel(LoadRAM));
  and and_1 (LoadRAM, ~DESHABILITAR_DISPATCHER, LoadRAMOn);  // AND_Gate
  Multiplexer #(.width(16), .enable("false")) multiplexer_5 (.in0(Addr), .in1(LAddr), .out(RAddr), .sel(LoadRAM));
  Multiplexer #(.width(4), .enable("false")) multiplexer_6 (.in0(Mask), .in1(LMask), .out(RMask), .sel(LoadRAM));
  Multiplexer #(.enable("false")) multiplexer_7 (.in0(CS), .in1(LW), .out(RCS), .sel(LoadRAM));
  Multiplexer #(.enable("false")) multiplexer_8 (.in0(R_W), .in1(LW), .out(R_R_W), .sel(LoadRAM));

  // Notes on the sheet:
  //   NO MODIFICAR
  //   Keyboard
endmodule

module RAM (
  input  [15:0] Address,
  input  [31:0] Data_In_0,
  input  [31:0] Data_In_1,
  input  [31:0] Data_In_2,
  input  [31:0] Data_In_3,
  input  [3:0] Mask,
  input  nRead_Write,
  input  Chip_Select,
  input  Reset,
  output [31:0] Data_Out_0,
  output [31:0] Data_Out_1,
  output [31:0] Data_Out_2,
  output [31:0] Data_Out_3,
  output [3:0] Read_Time,
  output [3:0] Write_Time
);

  wire and_2_out, and_3_out, and_4_out, and_5_out, and_6_out, and_7_out, and_8_out, and_9_out, Changed, CLK,
       comparator_2_eq, comparator_3_eq, comparator_4_eq, comparator_5_eq, comparator_6_eq, Count,
       demultiplexer_3_out0, Idle, Idle_q, Load, Load0, Load1, nand_1_out, or_1_out, or_2_out, or_3_out,
       or_4_out, or_5_out, or_6_out, or_7_out, or_8_out, or_9_out, or_10_out, Proc_q, Update_Mem, Zero_Time;
  wire [3:0] counter_1_q, multiplexer_1_out, subtractor_1_out;
  wire [31:0] register_1_q, register_2_q, register_3_q, register_4_q, register_5_q;

  // Probe on 4'b0011
  // Probe on 4'b0010
  Multiplexer #(.width(4), .enable("false")) multiplexer_1 (
    .in0(4'b0011), .in1(4'b0010), .out(multiplexer_1_out), .sel(nRead_Write));
  or or_1 (or_1_out, Idle, Update_Mem);
  or or_2 (or_2_out, ~Chip_Select, Reset);  // OR_Gate
  Subtractor #(.width(4)) subtractor_1 (.a(multiplexer_1_out), .b(4'b0010), .out(subtractor_1_out));  // open: bin, bout
  Demultiplexer #(.enable("false")) demultiplexer_1 (.out0(Idle), .out1(Load0), .in(Idle_q), .sel(Changed));
  D_Flip_Flop u_Idle (.clk(CLK), .D(or_1_out), .Q(Idle_q), .preset(or_2_out));  // open: Qn, en, reset
  // Probe on counter_1_q
  Counter #(.width(4), .max('hf)) counter_1 (
    .load(Load), .D(subtractor_1_out), .count(Count), .Q(counter_1_q), .clk(CLK), .clr(or_3_out));  // open: carry
  or or_3 (or_3_out, ~Chip_Select, Reset);  // OR_Gate
  Comparator #(.width(4), .mode("unsigned")) comparator_1 (
    .a(4'b0000), .b(counter_1_q), .eq(Zero_Time));  // open: gt, lt
  or or_4 (or_4_out, Count, Load0, Load1);
  Register #(.width(32)) register_1 (.D(Data_In_0), .en(Chip_Select), .Q(register_1_q), .clk(CLK), .clr(or_5_out));
  or or_5 (or_5_out, ~Chip_Select, Reset);  // OR_Gate
  Register #(.width(32)) register_2 (.D(Data_In_1), .en(Chip_Select), .Q(register_2_q), .clk(CLK), .clr(or_6_out));
  or or_6 (or_6_out, ~Chip_Select, Reset);  // OR_Gate
  Register #(.width(32)) register_3 (.D(Data_In_2), .en(Chip_Select), .Q(register_3_q), .clk(CLK), .clr(or_7_out));
  or or_7 (or_7_out, ~Chip_Select, Reset);  // OR_Gate
  Register #(.width(32)) register_4 (.D(Data_In_3), .en(Chip_Select), .Q(register_4_q), .clk(CLK), .clr(or_8_out));
  or or_8 (or_8_out, ~Chip_Select, Reset);  // OR_Gate
  Register #(.width(32)) register_5 (
    .D({{11{1'b1}}, nRead_Write, Mask, Address}), .en(Chip_Select), .Q(register_5_q), .clk(CLK),
    .clr(or_9_out));
  or or_9 (or_9_out, ~Chip_Select, Reset);  // OR_Gate
  D_Flip_Flop Proc (.clk(CLK), .D(or_4_out), .Q(Proc_q), .reset(or_10_out));  // open: Qn, preset, en
  or or_10 (or_10_out, ~Chip_Select, Reset);  // OR_Gate
  Demultiplexer #(.enable("false")) demultiplexer_2 (
    .out0(Count), .out1(Update_Mem), .in(demultiplexer_3_out0), .sel(Zero_Time));
  Demultiplexer #(.enable("false")) demultiplexer_3 (
    .out0(demultiplexer_3_out0), .out1(Load1), .in(Proc_q), .sel(Changed));
  Clock clock_1 (.out(CLK));
  Comparator #(.width(32)) comparator_2 (.a(register_1_q), .b(Data_In_0), .eq(comparator_2_eq));  // open: gt, lt
  Comparator #(.width(32)) comparator_3 (.a(register_2_q), .b(Data_In_1), .eq(comparator_3_eq));  // open: gt, lt
  Comparator #(.width(32)) comparator_4 (.a(register_3_q), .b(Data_In_2), .eq(comparator_4_eq));  // open: gt, lt
  Comparator #(.width(32)) comparator_5 (.a(register_4_q), .b(Data_In_3), .eq(comparator_5_eq));  // open: gt, lt
  Comparator #(.width(32)) comparator_6 (
    .a(register_5_q), .b({{11{1'b1}}, nRead_Write, Mask, Address}), .eq(comparator_6_eq));  // open: gt, lt
  nand nand_1 (nand_1_out, comparator_6_eq, comparator_2_eq, comparator_3_eq, comparator_4_eq, comparator_5_eq);
  and and_1 (Changed, nand_1_out, Chip_Select);
  or or_11 (Load, Count, Load1, Load0);
  and and_2 (and_2_out, Mask[0], Update_Mem, nRead_Write);
  and and_3 (and_3_out, Mask[1], Update_Mem, nRead_Write);
  and and_4 (and_4_out, Mask[2], Update_Mem, nRead_Write);
  and and_5 (and_5_out, Mask[3], Update_Mem, nRead_Write);
  RAM_part #(.addrWidth(16), .dataWidth(32), .bus("separate")) ram_1 (
    .addr(Address), .din(Data_In_0), .data(Data_Out_0), .str(and_2_out), .sel(Chip_Select), .clk(CLK),
    .ld(and_6_out), .clr(Reset));
  and and_6 (and_6_out, ~nRead_Write, Idle);  // AND_Gate
  RAM_part #(.addrWidth(16), .dataWidth(32), .bus("separate")) ram_2 (
    .addr(Address), .din(Data_In_1), .data(Data_Out_1), .str(and_3_out), .sel(Chip_Select), .clk(CLK),
    .ld(and_7_out), .clr(Reset));
  and and_7 (and_7_out, ~nRead_Write, Idle);  // AND_Gate
  RAM_part #(.addrWidth(16), .dataWidth(32), .bus("separate")) ram_3 (
    .addr(Address), .din(Data_In_2), .data(Data_Out_2), .str(and_4_out), .sel(Chip_Select), .clk(CLK),
    .ld(and_8_out), .clr(Reset));
  and and_8 (and_8_out, ~nRead_Write, Idle);  // AND_Gate
  RAM_part #(.addrWidth(16), .dataWidth(32), .bus("separate")) ram_4 (
    .addr(Address), .din(Data_In_3), .data(Data_Out_3), .str(and_5_out), .sel(Chip_Select), .clk(CLK),
    .ld(and_9_out), .clr(Reset));
  and and_9 (and_9_out, ~nRead_Write, Idle);  // AND_Gate

  assign Read_Time = 4'b0011;
  assign Write_Time = 4'b0010;

  // Other names for the same wires on the sheet: M0 = Mask[0]; M1 = Mask[1]; M2 = Mask[2]; M3 = Mask[3];
  //   RW = nRead_Write; CLR = Reset; CS = Chip_Select; Load2 = Count

  // Notes on the sheet:
  //   NO MODIFICAR
  //   excepto quizás los valores RT y WT
  //   BANK0
  //   BANK1
  //   BANK2
  //   BANK3
endmodule

module S_MIPS (
  input  Kbd_Available,
  input  [6:0] Kbd_ASCII_Data,
  input  [31:0] RAM_Out_0,
  input  [31:0] RAM_Out_1,
  input  Reset,
  input  [31:0] RAM_Out_2,
  input  Clock,
  input  [31:0] RAM_Out_3,
  input  [3:0] Read_Time,
  input  [3:0] Write_Time,
  output Kbd_Enable,
  output [15:0] Address,
  output Kbd_Clear,
  output TTY_Enable,
  output [6:0] TTY_ASCII_Data,
  output Stop,
  output [31:0] RAM_In_0,
  output [31:0] RAM_In_1,
  output [31:0] RAM_In_2,
  output [31:0] RAM_In_3,
  output [3:0] Mask,
  output nRead_Write,
  output Chip_Select
);

  wire AluInst, d_ff_1_q, enGI, enPC, enRF, getData, getIsnt, Halt, JmpInst, MemInst, or_1_out, or_2_out,
       ReadyData, ReadyInst, ReadyW, RInst, StackInst, Start, Tty, Write, WriteInst;
  wire [31:0] Address_t, data_path_1_out_15, DataIn, multiplexer_1_out, multiplexer_2_out, multiplexer_3_out,
       multiplexer_4_out, ram_interaction_1_out_14, ram_interaction_1_out_15, ram_interaction_1_out_16,
       ram_interaction_1_out_17;

  D_Flip_Flop #(.trigger("falling")) d_ff_1 (
    .clk(Clock), .D(getIsnt), .Q(d_ff_1_q), .en(or_1_out));  // open: Qn, preset, reset
  or or_1 (or_1_out, getIsnt, ReadyInst);
  Data_Path data_path_1 (
    .in_1(Clock), .out_10(Halt), .in_2(DataIn), .in_3(Reset), .out_12(Tty), .in_4(enPC), .out_13(AluInst),
    .in_5(enGI), .out_14(MemInst), .in_6(Kbd_Available), .out_16(RInst), .in_7(d_ff_1_q), .out_17(StackInst),
    .in_8(enRF), .out_18(JmpInst), .out_19(TTY_ASCII_Data), .in_9(Kbd_ASCII_Data), .out_20(WriteInst),
    .out_11(Address_t), .out_15(data_path_1_out_15));
  Multiplexer #(.width(32), .enable("false")) multiplexer_1 (
    .in0(RAM_Out_0), .in1(RAM_In_0), .out(multiplexer_1_out), .sel(Write));
  Multiplexer #(.width(32), .enable("false")) multiplexer_2 (
    .in0(RAM_Out_1), .in1(RAM_In_0), .out(multiplexer_2_out), .sel(Write));
  Multiplexer #(.width(32), .enable("false")) multiplexer_3 (
    .in0(RAM_Out_2), .in1(RAM_In_0), .out(multiplexer_3_out), .sel(Write));
  Multiplexer #(.width(32), .enable("false")) multiplexer_4 (
    .in0(RAM_Out_3), .in1(RAM_In_0), .out(multiplexer_4_out), .sel(Write));
  D_Flip_Flop #(.trigger("falling")) d_ff_2 (.clk(Clock), .D(Reset), .Q(Start));  // open: Qn, preset, en, reset
  RAM_Interaction ram_interaction_1 (
    .in_2(multiplexer_1_out), .in_8(multiplexer_2_out), .in_3(multiplexer_3_out), .in_9(multiplexer_4_out),
    .in_12(Address_t), .in_11(Read_Time), .in_13(Write_Time), .in_1(Clock), .in_4(Reset), .in_5(Write),
    .in_6(getIsnt), .in_7(getData), .out_18(Address), .out_21(Mask), .out_14(ram_interaction_1_out_14),
    .out_16(ram_interaction_1_out_16), .out_15(ram_interaction_1_out_15), .out_17(ram_interaction_1_out_17),
    .out_23(nRead_Write), .out_24(Chip_Select), .out_19(ReadyInst), .out_20(ReadyData), .out_22(ReadyW),
    .in_10(enGI));
  Switch switch_1 (.Input(data_path_1_out_15), .Output(RAM_In_0));
  or or_2 (or_2_out, StackInst, MemInst);
  Multiplexer #(.select(2), .width(32), .enable("false")) multiplexer_5 (
    .in0(ram_interaction_1_out_14), .in1(ram_interaction_1_out_16), .in2(ram_interaction_1_out_15),
    .in3(ram_interaction_1_out_17), .out(DataIn), .sel(Address_t[3:2]));
  Control_Unit control_unit_1 (
    .in_1(Clock), .in_2(Start), .in_3(ReadyInst), .in_4(AluInst), .in_5(RInst), .in_6(Reset), .in_7(Tty),
    .in_8(ReadyData), .in_9(JmpInst), .in_10(or_2_out), .in_11(WriteInst), .in_12(ReadyW), .out_13(enRF),
    .out_14(enPC), .out_15(Stop), .out_16(getData), .out_17(getIsnt), .out_18(enGI), .out_19(TTY_Enable),
    .out_20(Kbd_Enable), .out_21(Write));

  assign Kbd_Clear = Reset;
  assign RAM_In_1 = RAM_In_0;
  assign RAM_In_2 = RAM_In_0;
  assign RAM_In_3 = RAM_In_0;

  // Other names for the same wires on the sheet: CLK = Clock; CS = Chip_Select; KBD_AVAIL = Kbd_Available;
  //   CLR = Reset; KBD_CLR = Reset; KBD_DATA[6:0] = Kbd_ASCII_Data; RAM_A[15:0] = Address; RAM_MASK[3:0] = Mask;
  //   RAM_OUTPUT_0[31:0] = RAM_Out_0; RAM_OUTPUT_1[31:0] = RAM_Out_1; RAM_OUTPUT_2[31:0] = RAM_Out_2;
  //   RAM_OUTPUT_3[31:0] = RAM_Out_3; RAM_INPUT_0[31:0] = RAM_In_0; RAM_INPUT_1[31:0] = RAM_In_0;
  //   RAM_INPUT_2[31:0] = RAM_In_0; RAM_INPUT_3[31:0] = RAM_In_0; ROut[31:0] = RAM_In_0; RW = nRead_Write;
  //   TTY_DATA[6:0] = TTY_ASCII_Data

  // Notes on the sheet:
  //   RAM ADDRESS
  //   DATA FROM RAM
  //   DATA TO RAM
  //   DATA WRITE MASK
  //   RAM TIMING
  //   RAM CONTROL
  //   KEYBOARD
  //   TTY
  //   SEQUENCING
endmodule

module RAM_Dispatcher (
  input  [3:0] WriteTime,
  input  Clock,
  input  CLR,
  output [31:0] Data,
  output [15:0] Address,
  output [3:0] Mask,
  output Finished,
  output Write
);

  wire demultiplexer_2_out1, demultiplexer_3_out1, End, IDLE_q, IncAddr, Load, or_1_out, or_2_out, While_q,
       WriteEnd;
  wire [3:0] counter_1_q;
  wire [31:0] CurrentAddress_q;

  Counter #(.width(32), .max('hffffffff)) CurrentAddress (
    .count(IncAddr), .Q({CurrentAddress_q[31:18], Address, CurrentAddress_q[1:0]}), .clk(Clock), .clr(CLR));  // open: load, D, carry
  or or_1 (or_1_out, IncAddr, demultiplexer_3_out1, Finished);
  D_Flip_Flop IDLE (.clk(Clock), .D(or_1_out), .Q(IDLE_q), .preset(CLR));  // open: Qn, en, reset
  Demultiplexer #(.enable("false")) demultiplexer_1 (.out0(Load), .out1(Finished), .in(IDLE_q), .sel(End));
  D_Flip_Flop While (.clk(Clock), .D(or_2_out), .Q(While_q), .reset(CLR));  // open: Qn, preset, en
  or or_2 (or_2_out, Write, Load);
  RAM_part #(.addrWidth(18), .dataWidth(32)) ram_1 (
    .addr({Address, CurrentAddress_q[1:0]}), .data(Data), .clk(Clock));  // open: sel, ld, clr
  Demultiplexer #(.enable("false")) demultiplexer_2 (
    .out0(Write), .out1(demultiplexer_2_out1), .in(While_q), .sel(WriteEnd));
  Decoder #(.select(2)) decoder_1 (
    .out0(Mask[0]), .out1(Mask[1]), .out2(Mask[2]), .out3(Mask[3]), .sel(CurrentAddress_q[1:0]));  // open: en
  Demultiplexer #(.enable("false")) demultiplexer_3 (
    .out0(IncAddr), .out1(demultiplexer_3_out1), .in(demultiplexer_2_out1), .sel(End));
  Counter #(.width(4), .max('hf)) counter_1 (
    .load(Load), .D(WriteTime), .count(Write), .Q(counter_1_q), .clk(Clock));  // open: carry, clr
  Comparator #(.width(32)) comparator_1 (.a(Data), .b({32{1'b1}}), .eq(End));  // open: gt, lt
  Comparator #(.width(4)) comparator_2 (.a(4'b0000), .b(counter_1_q), .eq(WriteEnd));  // open: gt, lt

  // Other names for the same wires on the sheet: CLK = Clock; Count = Write; WT[3:0] = WriteTime
endmodule

module Data_Path (
  input  in_1,
  input  [31:0] in_2,
  input  in_3,
  input  in_4,
  input  in_5,
  input  in_6,
  input  in_7,
  input  in_8,
  input  [6:0] in_9,
  output out_10,
  output [31:0] out_11,
  output out_12,
  output out_13,
  output out_14,
  output [31:0] out_15,
  output out_16,
  output out_17,
  output out_18,
  output [6:0] out_19,
  output out_20
);

  wire beq, bgtz, blez, bltz, bne, inmediate, j, jr, kbd, lw, mfhi, mflo, nop, onALU, pop, push, rnd,
       \signed , sw;
  wire [2:0] RFsel;
  wire [3:0] instruction_decoder_1_opalu;
  wire [4:0] instruction_decoder_1_da, instruction_decoder_1_sa, instruction_decoder_1_sb;
  wire [15:0] Constante;
  wire [25:0] Destino;
  wire [31:0] branch_control_1_out_13, DI, extKBD, get_instruction_1_out_5, Hi, k, Lo, multiplexer_3_out,
       program_counter_1_output, random, result, Rt, SP;
  wire [31:7] Rs;

  Get_Instruction get_instruction_1 (
    .in_1(in_1), .in_2(in_2), .in_3(in_3), .out_5(get_instruction_1_out_5), .in_4(in_5));
  Instruction_Decoder instruction_decoder_1 (
    .Instruction(get_instruction_1_out_5), .OpALU(instruction_decoder_1_opalu),
    .SA(instruction_decoder_1_sa), .out_7(k), .SB(instruction_decoder_1_sb), .out_13(inmediate),
    .DA(instruction_decoder_1_da), .out_18(\signed ), .out_3(bltz), .out_8(bgtz), .out_11(blez),
    .out_14(bne), .out_19(beq), .out_22(j), .out_25(jr), .out_5(Constante), .out_16(Destino), .out_4(nop),
    .out_9(lw), .out_12(sw), .out_15(pop), .out_20(push), .out_23(mfhi), .out_26(mflo), .out_28(out_10),
    .out_27(kbd), .out_29(out_12), .out_30(rnd), .out_24(onALU));  // open: out_21
  Branch_Control branch_control_1 (
    .in_1(bltz), .in_2(Constante), .in_3(bgtz), .in_4(program_counter_1_output), .in_5(Rt), .in_6(blez),
    .in_7(Destino), .in_8(bne), .in_9(beq), .in_10({Rs, out_19}), .in_11(j), .in_12(jr),
    .out_13(branch_control_1_out_13));
  Program_Counter program_counter_1 (
    .in_2(in_3), .in_3(in_4), .in_4(branch_control_1_out_13), .Output(program_counter_1_output), .in_1(in_1));
  Multiplexer #(.select(3), .width(32), .enable("false")) multiplexer_1 (
    .in0(result), .in1(in_2), .in2(Hi), .in3(Lo), .in4(random), .in5(extKBD), .out(DI), .sel(RFsel));  // open: in6, in7
  MemoryAddress memoryaddress_1 (
    .in_1(result), .in_2(pop), .in_3(push), .in_4(lw), .in_5(program_counter_1_output), .in_6(sw),
    .in_7(in_7), .in_8(SP), .Output(out_11));
  or or_1 (RFsel[0], lw, pop, mflo, kbd);
  or or_2 (RFsel[1], mflo, mfhi);
  or or_3 (RFsel[2], rnd, kbd);
  assign extKBD = {{25{1'b0}}, in_9};  // Bit_Extender bit_extender_1
  Random #(.width(32)) random_1 (.clk(in_1), .next(rnd), .out(random));  // open: clr
  Register_File register_file_1 (
    .in_1(in_1), .in_2(in_3), .in_3(instruction_decoder_1_sa), .Input(DI), .in_5(in_8),
    .in_6(instruction_decoder_1_da), .in_7(instruction_decoder_1_sb), .A({Rs, out_19}), .B(Rt), .in_8(pop),
    .in_9(push), .in_10(in_4), .out_13(SP));
  Multiplexer #(.width(32), .enable("false")) multiplexer_2 (.in0({Rs, out_19}), .in1(Rt), .out(out_15), .sel(sw));
  or or_4 (out_20, push, sw);
  or or_5 (out_17, push, pop);
  or or_6 (out_14, lw, sw);
  and and_1 (out_13, onALU, ~lw, ~sw);  // AND_Gate
  ALU alu_1 (
    .Op(instruction_decoder_1_opalu), .A({Rs, out_19}), .B(multiplexer_3_out), .\signed (\signed ),
    .Clk(in_1), .result(result), .Lo(Lo), .Hi(Hi));
  Multiplexer #(.width(32), .enable("false")) multiplexer_3 (
    .in0(Rt), .in1(k), .out(multiplexer_3_out), .sel(inmediate));
  or or_7 (out_16, rnd, mfhi, mflo, kbd, out_12);
  or or_8 (out_18, bgtz, beq, bne, blez, bltz, jr, j, nop);

  // Other names for the same wires on the sheet: Address[31:0] = out_11; AluInst = out_13; Clk = in_1;
  //   direction[31:0] = in_2; enGI = in_5; enPC = in_4; enRF = in_8; halt = out_10; JmpInst = out_18;
  //   kbd_data[6:0] = in_9; kbdAva = in_6; MemInst = out_14; NextInst = in_7; reset = in_3; RInst = out_16;
  //   ROut[31:0] = out_15; Rs[6:0] = out_19; TtyData[6:0] = out_19; StackInst = out_17; tty = out_12;
  //   WriteInst = out_20

  // Notes on the sheet:
  //   Entradas
  //   Dato a escribir en el RF
  //   KBD
  //   RND
  //   Selector de la entrada RF
  //   Salidas
  //   ROut
  //   Identificando Instrucciones
  //   TTY
endmodule

module ALU (
  input  [3:0] Op,
  input  [31:0] A,
  input  [31:0] B,
  input  \signed ,
  input  Clk,
  output [31:0] result,
  output [31:0] Lo,
  output [31:0] Hi
);

  wire div, en, mult;
  wire [31:0] add, \and , Cocient, MultHi, multiplexer_2_out, multiplexer_3_out, MultLo, \nor , \or ,
       Remainder, slt, sub, \xor ;

  Adder #(.width(32)) adder_1 (.a(A), .b(B), .out(add));  // open: cin, cout
  Subtractor #(.width(32)) subtractor_1 (.a(A), .b(B), .out(sub));  // open: bin, bout
  assign \and  = A & B;  // AND_Gate and_1, 32 bits wide
  assign \or  = A | B;  // OR_Gate or_1, 32 bits wide
  Multiplier multiplier_1 (.A(A), .B(B), .\signed (\signed ), .LoResult(MultLo), .HiResult(MultHi));
  Set_Less_Than set_less_than_1 (.A(A), .B(B), .\signed (\signed ), .result(slt));
  assign \xor  = A ^ B;  // XOR_Gate xor_1, 32 bits wide
  assign \nor  = ~(A | B);  // NOR_Gate nor_1, 32 bits wide
  Dividier dividier_1 (.A(A), .B(B), .\signed (\signed ), .Lo(Cocient), .Hi(Remainder));
  Multiplexer #(.select(4), .width(32), .enable("false")) multiplexer_1 (
    .in1(sub), .in2(\and ), .in3(\or ), .in4(\nor ), .in5(\xor ), .in6(slt), .in9(add), .out(result), .sel(Op));  // open: in0, in7, in8, in10, in11, in12, in13, in14, in15
  Multiplexer #(.width(32), .enable("false")) multiplexer_2 (
    .in0(MultLo), .in1(Cocient), .out(multiplexer_2_out), .sel(div));
  Register #(.width(32)) u_Lo (.D(multiplexer_2_out), .en(en), .Q(Lo), .clk(Clk));  // open: clr
  Multiplexer #(.width(32), .enable("false")) multiplexer_3 (
    .in0(MultHi), .in1(Remainder), .out(multiplexer_3_out), .sel(div));
  Register #(.width(32)) u_Hi (.D(multiplexer_3_out), .en(en), .Q(Hi), .clk(Clk));  // open: clr
  Comparator #(.width(4)) comparator_1 (.a(Op), .b(4'b0111), .eq(mult));  // open: gt, lt
  Comparator #(.width(4)) comparator_2 (.a(Op), .b(4'b1000), .eq(div));  // open: gt, lt
  or or_2 (en, mult, div);
endmodule

module Multiplier (
  input  [31:0] A,
  input  [31:0] B,
  input  \signed ,
  output [31:0] LoResult,
  output [31:0] HiResult
);

  wire adder_1_cout, sel, signA, signB, xor_1_out;
  wire [31:0] A_prime, B_prime, bit_extender_1_out, Hi, Hi_prime, Lo, Lo_prime, not_1_out, not_2_out;

  Complement_A2 complement_a2_1 (.A(A), .\signed (\signed ), .result(A_prime), .signA(signA));
  assign not_1_out = ~Lo;  // NOT_Gate not_1, 32 bits wide
  Adder #(.width(32)) adder_1 (.a(not_1_out), .b(32'h1), .out(Lo_prime), .cout(adder_1_cout));  // open: cin
  assign bit_extender_1_out = {{31{1'b0}}, adder_1_cout};  // Bit_Extender bit_extender_1
  assign not_2_out = ~Hi;  // NOT_Gate not_2, 32 bits wide
  Complement_A2 complement_a2_2 (.A(B), .\signed (\signed ), .result(B_prime), .signA(signB));
  Adder #(.width(32)) adder_2 (.a(bit_extender_1_out), .b(not_2_out), .out(Hi_prime));  // open: cin, cout
  Multiplexer #(.width(32), .enable("false")) multiplexer_1 (.in0(Lo), .in1(Lo_prime), .out(LoResult), .sel(sel));
  Multiplier_part #(.width(32)) multiplier_1 (.a(A_prime), .b(B_prime), .out(Lo), .cout(Hi));  // open: cin
  Multiplexer #(.width(32), .enable("false")) multiplexer_2 (.in0(Hi), .in1(Hi_prime), .out(HiResult), .sel(sel));
  xor xor_1 (xor_1_out, signA, signB);
  and and_1 (sel, \signed , xor_1_out);
endmodule

module Complement_A2 (
  input  [31:0] A,
  input  \signed ,
  output [31:0] result,
  output signA
);

  wire and_1_out;
  wire [31:0] negator_1_out;

  Negator #(.width(32)) negator_1 (.in(A), .out(negator_1_out));
  and and_1 (and_1_out, A[31], \signed );
  Multiplexer #(.width(32), .enable("false")) multiplexer_1 (
    .in0(A), .in1(negator_1_out), .out(result), .sel(and_1_out));

  assign signA = A[31];
endmodule

module Dividier (
  input  [31:0] A,
  input  [31:0] B,
  input  \signed ,
  output [31:0] Lo,
  output [31:0] Hi
);

  wire sel, signA, signB, xor_1_out;
  wire [31:0] A_prime, B_prime, divider_1_out, negator_1_out;

  Complement_A2 complement_a2_1 (.A(A), .\signed (\signed ), .result(A_prime), .signA(signA));
  Complement_A2 complement_a2_2 (.A(B), .\signed (\signed ), .result(B_prime), .signA(signB));
  Divider #(.width(32)) divider_1 (.a(A_prime), .b(B_prime), .out(divider_1_out), .rem(Hi));  // open: upper
  Negator #(.width(32)) negator_1 (.in(divider_1_out), .out(negator_1_out));
  Multiplexer #(.width(32), .enable("false")) multiplexer_1 (
    .in0(divider_1_out), .in1(negator_1_out), .out(Lo), .sel(sel));
  xor xor_1 (xor_1_out, signA, signB);
  and and_1 (sel, \signed , xor_1_out);
endmodule

module Set_Less_Than (
  input  [31:0] A,
  input  [31:0] B,
  input  \signed ,
  output [31:0] result
);

  wire and_1_out, and_2_out, comparator_1_lt, comparator_2_lt, or_1_out;

  Comparator #(.width(32)) comparator_1 (.a(A), .b(B), .lt(comparator_1_lt));  // open: gt, eq
  Comparator #(.width(32), .mode("unsigned")) comparator_2 (.a(A), .b(B), .lt(comparator_2_lt));  // open: gt, eq
  and and_1 (and_1_out, comparator_1_lt, \signed );
  and and_2 (and_2_out, ~\signed , comparator_2_lt);  // AND_Gate
  or or_1 (or_1_out, and_1_out, and_2_out);
  assign result = {{31{1'b0}}, or_1_out};  // Bit_Extender bit_extender_1
endmodule

module Register_File (
  input  in_1,
  input  in_2,
  input  [4:0] in_3,
  input  [31:0] Input,
  input  in_5,
  input  [4:0] in_6,
  input  [4:0] in_7,
  input  in_8,
  input  in_9,
  input  in_10,
  output [31:0] A,
  output [31:0] B,
  output [31:0] out_13
);

  wire en31, L0, L1, L2, L3, L4, L5, L6, L7, L8, L9, L10, L11, L12, L13, L14, L15, L16, L17, L18, L19, L20,
       L21, L22, L23, L24, L25, L26, L27, L28, L29, L30, L31, or_1_out, or_2_out;
  wire [31:0] adder_1_out, multiplexer_1_out, multiplexer_3_out, multiplexer_4_out, R0, R1, R2, R3, R4, R5,
       R6, R7, R8, R9, R10, R11, R12, R13, R14, R15, R16, R17, R18, R19, R20, R21, R22, R23, R24, R25, R26,
       R27, R28, R29, R30, subtractor_1_out;

  Demultiplexer #(.select(5), .enable("false")) demultiplexer_1 (
    .out0(L0), .out1(L1), .out2(L2), .out3(L3), .out4(L4), .out5(L5), .out6(L6), .out7(L7), .out8(L8),
    .out9(L9), .out10(L10), .out11(L11), .out12(L12), .out13(L13), .out14(L14), .out15(L15), .out16(L16),
    .out17(L17), .out18(L18), .out19(L19), .out20(L20), .out21(L21), .out22(L22), .out23(L23), .out24(L24),
    .out25(L25), .out26(L26), .out27(L27), .out28(L28), .out29(L29), .out30(L30), .out31(L31), .in(in_5),
    .sel(in_6));
  Register #(.width(32)) u_R0 (.D({32{1'b0}}), .en(L0), .Q(R0), .clk(in_1), .clr(in_2));
  Register #(.width(32)) u_R6 (.D(Input), .en(L6), .Q(R6), .clk(in_1), .clr(in_2));
  Register #(.width(32)) u_R12 (.D(Input), .en(L12), .Q(R12), .clk(in_1), .clr(in_2));
  Register #(.width(32)) u_R18 (.D(Input), .en(L18), .Q(R18), .clk(in_1), .clr(in_2));
  Register #(.width(32)) u_R24 (.D(Input), .en(L24), .Q(R24), .clk(in_1), .clr(in_2));
  Register #(.width(32)) u_R30 (.D(Input), .en(L30), .Q(R30), .clk(in_1), .clr(in_2));
  Register #(.width(32)) u_R1 (.D(Input), .en(L1), .Q(R1), .clk(in_1), .clr(in_2));
  Register #(.width(32)) u_R7 (.D(Input), .en(L7), .Q(R7), .clk(in_1), .clr(in_2));
  Register #(.width(32)) u_R13 (.D(Input), .en(L13), .Q(R13), .clk(in_1), .clr(in_2));
  Register #(.width(32)) u_R19 (.D(Input), .en(L19), .Q(R19), .clk(in_1), .clr(in_2));
  Register #(.width(32)) u_R25 (.D(Input), .en(L25), .Q(R25), .clk(in_1), .clr(in_2));
  Subtractor #(.width(32)) subtractor_1 (.a(out_13), .b(32'h4), .out(subtractor_1_out));  // open: bin, bout
  Adder #(.width(32)) adder_1 (.a(32'h4), .b(out_13), .out(adder_1_out));  // open: cin, cout
  Register #(.width(32)) u_R2 (.D(Input), .en(L2), .Q(R2), .clk(in_1), .clr(in_2));
  Register #(.width(32)) u_R8 (.D(Input), .en(L8), .Q(R8), .clk(in_1), .clr(in_2));
  Register #(.width(32)) u_R14 (.D(Input), .en(L14), .Q(R14), .clk(in_1), .clr(in_2));
  Register #(.width(32)) u_R20 (.D(Input), .en(L20), .Q(R20), .clk(in_1), .clr(in_2));
  Register #(.width(32)) u_R26 (.D(Input), .en(L26), .Q(R26), .clk(in_1), .clr(in_2));
  Multiplexer #(.width(32), .enable("false")) multiplexer_1 (
    .in0(subtractor_1_out), .in1(adder_1_out), .out(multiplexer_1_out), .sel(in_8));
  Multiplexer #(.select(5), .width(32), .enable("false")) multiplexer_2 (
    .in0(R0), .in1(R1), .in2(R2), .in3(R3), .in4(R4), .in5(R5), .in6(R6), .in7(R7), .in8(R8), .in9(R9),
    .in10(R10), .in11(R11), .in12(R12), .in13(R13), .in14(R14), .in15(R15), .in16(R16), .in17(R17),
    .in18(R18), .in19(R19), .in20(R20), .in21(R21), .in22(R22), .in23(R23), .in24(R24), .in25(R25),
    .in26(R26), .in27(R27), .in28(R28), .in29(R29), .in30(R30), .in31(out_13), .out(A), .sel(in_3));
  Multiplexer #(.width(32), .enable("false")) multiplexer_3 (
    .in0(multiplexer_1_out), .in1({32{1'b1}}), .out(multiplexer_3_out), .sel(in_2));
  Register #(.width(32)) u_R3 (.D(Input), .en(L3), .Q(R3), .clk(in_1), .clr(in_2));
  Register #(.width(32)) u_R9 (.D(Input), .en(L9), .Q(R9), .clk(in_1), .clr(in_2));
  Register #(.width(32)) u_R15 (.D(Input), .en(L15), .Q(R15), .clk(in_1), .clr(in_2));
  Register #(.width(32)) u_R21 (.D(Input), .en(L21), .Q(R21), .clk(in_1), .clr(in_2));
  Register #(.width(32)) u_R27 (.D(Input), .en(L27), .Q(R27), .clk(in_1), .clr(in_2));
  Multiplexer #(.width(32), .enable("false")) multiplexer_4 (
    .in0(multiplexer_3_out), .in1(Input), .out(multiplexer_4_out), .sel(L31));
  or or_1 (or_1_out, en31, L31, in_2);
  Register #(.width(32)) register_1 (.D(multiplexer_4_out), .en(or_1_out), .Q(out_13), .clk(in_1));  // open: clr
  Multiplexer #(.select(5), .width(32), .enable("false")) multiplexer_5 (
    .in0(R0), .in1(R1), .in2(R2), .in3(R3), .in4(R4), .in5(R5), .in6(R6), .in7(R7), .in8(R8), .in9(R9),
    .in10(R10), .in11(R11), .in12(R12), .in13(R13), .in14(R14), .in15(R15), .in16(R16), .in17(R17),
    .in18(R18), .in19(R19), .in20(R20), .in21(R21), .in22(R22), .in23(R23), .in24(R24), .in25(R25),
    .in26(R26), .in27(R27), .in28(R28), .in29(R29), .in30(R30), .in31(out_13), .out(B), .sel(in_7));
  Register #(.width(32)) u_R4 (.D(Input), .en(L4), .Q(R4), .clk(in_1), .clr(in_2));
  Register #(.width(32)) u_R10 (.D(Input), .en(L10), .Q(R10), .clk(in_1), .clr(in_2));
  Register #(.width(32)) u_R16 (.D(Input), .en(L16), .Q(R16), .clk(in_1), .clr(in_2));
  Register #(.width(32)) u_R22 (.D(Input), .en(L22), .Q(R22), .clk(in_1), .clr(in_2));
  Register #(.width(32)) u_R28 (.D(Input), .en(L28), .Q(R28), .clk(in_1), .clr(in_2));
  or or_2 (or_2_out, in_9, in_8);
  and and_1 (en31, in_10, or_2_out);
  Register #(.width(32)) u_R5 (.D(Input), .en(L5), .Q(R5), .clk(in_1), .clr(in_2));
  Register #(.width(32)) u_R11 (.D(Input), .en(L11), .Q(R11), .clk(in_1), .clr(in_2));
  Register #(.width(32)) u_R17 (.D(Input), .en(L17), .Q(R17), .clk(in_1), .clr(in_2));
  Register #(.width(32)) u_R23 (.D(Input), .en(L23), .Q(R23), .clk(in_1), .clr(in_2));
  Register #(.width(32)) u_R29 (.D(Input), .en(L29), .Q(R29), .clk(in_1), .clr(in_2));

  // Other names for the same wires on the sheet: Clk = in_1; DA[4:0] = in_6; enPC = in_10; pop = in_8; push = in_9;
  //   R31[31:0] = out_13; Reset = in_2; RW = in_5; SA[4:0] = in_3; SB[4:0] = in_7
endmodule

module Instruction_Decoder (
  input  [31:0] Instruction,
  output [3:0] OpALU,
  output out_3,
  output out_4,
  output [15:0] out_5,
  output [4:0] SA,
  output [31:0] out_7,
  output out_8,
  output out_9,
  output [4:0] SB,
  output out_11,
  output out_12,
  output out_13,
  output out_14,
  output out_15,
  output [25:0] out_16,
  output [4:0] DA,
  output out_18,
  output out_19,
  output out_20,
  output out_21,
  output out_22,
  output out_23,
  output out_24,
  output out_25,
  output out_26,
  output out_27,
  output out_28,
  output out_29,
  output out_30
);

  wire add, addi, \and , andi, comparator_1_eq, div, divu, mult, mulu, \nor , \or , or_4_out, ori, read0,
       read1, slt, slti, sltiu, sltu, sub, \xor , xori;
  wire [31:0] concat0, concat1;

  TipoR tipor_1 (
    .in_1(Instruction[31:26]), .out_3(out_4), .out_4(sub), .out_5(\nor ), .out_6(\xor ), .out_7(div),
    .out_8(out_26), .out_9(out_27), .out_10(out_28), .out_11(\and ), .out_12(slt), .out_13(mult),
    .out_14(divu), .out_15(out_15), .out_16(out_25), .in_2(Instruction[5:0]), .out_17(add), .out_18(\or ),
    .out_19(sltu), .out_20(mulu), .out_21(out_23), .out_22(out_30), .out_23(out_20), .out_24(out_29),
    .out_25(read0));
  nor nor_1 (out_18, sltu, sltiu, mulu, divu);
  Multiplexer #(.width(5), .enable("false")) multiplexer_1 (
    .in0(Instruction[15:11]), .in1(Instruction[20:16]), .out(DA), .sel(out_13));
  or or_1 (OpALU[0], sub, \or , ori, \xor , xori, mult, mulu, add, addi);
  TipoI tipoi_1 (
    .in_1(Instruction[31:26]), .out_2(addi), .out_3(slti), .out_4(sltiu), .out_5(andi), .out_7(ori),
    .out_8(xori), .out_9(out_9), .out_10(out_12), .out_12(out_19), .out_13(out_14), .out_14(out_11),
    .out_15(out_8), .out_16(out_3), .out_6(out_13), .out_11(read1));
  or or_2 (OpALU[1], \and , andi, \or , ori, mult, mulu, slt, sltu, slti, sltiu);
  assign concat0 = {{16{Instruction[15]}}, Instruction[15:0]};  // Bit_Extender bit_extender_1
  assign concat1 = {{16{1'b0}}, Instruction[15:0]};  // Bit_Extender bit_extender_2
  nor nor_2 (out_21, read0, read1, out_22);
  or or_3 (OpALU[2], \nor , \xor , xori, mult, mulu, slt, sltu, slti, sltiu);
  Multiplexer #(.width(32), .enable("false")) multiplexer_2 (.in0(concat0), .in1(concat1), .out(out_7), .sel(or_4_out));
  or or_4 (or_4_out, andi, ori, xori);
  and and_1 (out_22, ~Instruction[26], Instruction[27], ~Instruction[28], ~Instruction[29], ~Instruction[30], ~Instruction[31]);  // AND_Gate
  or or_5 (OpALU[3], div, divu, add, addi);
  Comparator #(.width(4)) comparator_1 (.a(OpALU), .b(4'b0000), .eq(comparator_1_eq));  // open: gt, lt
  not not_1 (out_24, comparator_1_eq);

  assign out_5 = Instruction[15:0];
  assign out_16 = Instruction[25:0];
  assign SA = Instruction[25:21];
  assign SB = Instruction[20:16];

  // Other names for the same wires on the sheet: beq = out_19; bgtz = out_8; blez = out_11; bltz = out_3;
  //   bne = out_14; halt = out_28; inmediate = out_13; Constante[15:0] = Instruction[15:0];
  //   Destino[25:0] = Instruction[25:0]; Fun_Code[5:0] = Instruction[5:0]; x[4:0] = Instruction[10:6];
  //   Rd[4:0] = Instruction[15:11]; Rt[4:0] = Instruction[20:16]; Rs[4:0] = Instruction[25:21];
  //   Op_Code[5:0] = Instruction[31:26]; j = out_22; jr = out_25; k_ALU[31:0] = out_7; kbd = out_27; lw = out_9;
  //   mfhi = out_23; mflo = out_26; nop = out_4; onALU = out_24; _0 = OpALU[0]; _1 = OpALU[1]; _2 = OpALU[2];
  //   _3 = OpALU[3]; pop = out_15; push = out_20; R_W = out_21; rnd = out_30; signed = out_18; sw = out_12;
  //   tty = out_29

  // Notes on the sheet:
  //   Signo Op
  //   Selector del registro a escribir
  //   Decodificar Op ALU
  //   Salidas
  //   K-ALU
  //   Verificando Op de lectura
  //   Tipo J
  //   OnALU
endmodule

module TipoR (
  input  [5:0] in_1,
  input  [5:0] in_2,
  output out_3,
  output out_4,
  output out_5,
  output out_6,
  output out_7,
  output out_8,
  output out_9,
  output out_10,
  output out_11,
  output out_12,
  output out_13,
  output out_14,
  output out_15,
  output out_16,
  output out_17,
  output out_18,
  output out_19,
  output out_20,
  output out_21,
  output out_22,
  output out_23,
  output out_24,
  output out_25
);

  wire and_1_out, and_2_out, and_15_out, and_16_out, and_37_out, FH000, FH001, FH010, FH011, FH100, FH101,
       FH111, FL000, FL001, FL010, FL011, FL100, FL101, FL111, Op0, Op1, Op10, Read0;

  and and_1 (and_1_out, Op0, FH010);
  and and_2 (and_2_out, Op1, FH000);
  and and_3 (FL000, ~in_2[0], ~in_2[1], ~in_2[2]);  // AND_Gate
  and and_4 (FH000, ~in_2[3], ~in_2[4], ~in_2[5]);  // AND_Gate
  and and_5 (FL100, ~in_2[0], ~in_2[1], in_2[2]);  // AND_Gate
  and and_6 (FH100, ~in_2[3], ~in_2[4], in_2[5]);  // AND_Gate
  and and_7 (out_3, Op0, FL000, FH000);
  and and_8 (out_10, Op1, FL111, FH111);
  and and_9 (Op0, ~in_1[0], ~in_1[1], ~in_1[2], ~in_1[3], ~in_1[4], ~in_1[5]);  // AND_Gate
  and and_10 (out_21, FL000, and_1_out);
  and and_11 (out_8, FL010, and_1_out);
  and and_12 (out_15, FL000, Op10, FH000);
  and and_13 (out_22, FL010, and_2_out);
  and and_14 (out_9, and_2_out, FL100);
  and and_15 (and_15_out, FH100, Op0);
  and and_16 (and_16_out, Op0, FH101);
  and and_17 (FL001, in_2[0], ~in_2[1], ~in_2[2]);  // AND_Gate
  and and_18 (FH001, in_2[3], ~in_2[4], ~in_2[5]);  // AND_Gate
  and and_19 (FL101, in_2[0], ~in_2[1], in_2[2]);  // AND_Gate
  and and_20 (FH101, in_2[3], ~in_2[4], in_2[5]);  // AND_Gate
  and and_21 (Op10, ~in_1[0], ~in_1[1], ~in_1[2], in_1[3], in_1[4], in_1[5]);  // AND_Gate
  and and_22 (out_17, FL000, and_15_out);
  and and_23 (out_4, FL010, and_15_out);
  and and_24 (out_11, FL100, and_15_out);
  and and_25 (out_18, FL101, and_15_out);
  and and_26 (out_5, FL111, and_15_out);
  and and_27 (out_12, FL010, and_16_out);
  and and_28 (out_19, FL011, and_16_out);
  and and_29 (out_6, FL000, and_16_out);
  and and_30 (out_16, Op0, FH001, FL000);
  and and_31 (out_23, Op10, FH000, FL001);
  and and_32 (out_24, FH000, FL001, Op1);
  and and_33 (FL010, ~in_2[0], in_2[1], ~in_2[2]);  // AND_Gate
  and and_34 (FH010, ~in_2[3], in_2[4], ~in_2[5]);  // AND_Gate
  and and_35 (FL111, in_2[0], in_2[1], in_2[2]);
  and and_36 (FH111, in_2[3], in_2[4], in_2[5]);
  and and_37 (and_37_out, FH011, Op0);
  and and_38 (Op1, in_1[0], in_1[1], in_1[2], in_1[3], in_1[4], in_1[5]);
  and and_39 (out_13, FL000, and_37_out);
  and and_40 (out_20, FL001, and_37_out);
  and and_41 (out_7, and_37_out, FL010);
  and and_42 (out_14, and_37_out, FL011);
  or or_1 (out_25, out_3, Read0, out_16);
  or or_2 (Read0, out_13, out_20, out_7, out_14);
  and and_43 (FL011, in_2[0], in_2[1], ~in_2[2]);  // AND_Gate
  and and_44 (FH011, in_2[3], in_2[4], ~in_2[5]);  // AND_Gate

  // Other names for the same wires on the sheet: add = out_17; and = out_11; div = out_7; divu = out_14;
  //   Fun_Code[5:0] = in_2; halt = out_10; jr = out_16; kbd = out_9; mfhi = out_21; mflo = out_8; mult = out_13;
  //   mulu = out_20; nop = out_3; nor = out_5; Op_Code[5:0] = in_1; or = out_18; pop = out_15; push = out_23;
  //   read = out_25; rnd = out_22; slt = out_12; sltu = out_19; sub = out_4; tty = out_24; xor = out_6

  // Notes on the sheet:
  //   Etiquetas TipoR
  //   Decodificar
  //   Op Lectura
endmodule

module TipoI (
  input  [5:0] in_1,
  output out_2,
  output out_3,
  output out_4,
  output out_5,
  output out_6,
  output out_7,
  output out_8,
  output out_9,
  output out_10,
  output out_11,
  output out_12,
  output out_13,
  output out_14,
  output out_15,
  output out_16
);

  wire addi0, and_19_out, OH000, OH001, OH100, OH101, OL000, OL001, OL010, OL011, OL100, OL101, OL110, OL111,
       read0;

  and and_1 (OL000, ~in_1[0], ~in_1[1], ~in_1[2]);  // AND_Gate
  and and_2 (OH000, ~in_1[3], ~in_1[4], ~in_1[5]);  // AND_Gate
  and and_3 (OL100, ~in_1[0], ~in_1[1], in_1[2]);  // AND_Gate
  and and_4 (OH100, ~in_1[3], ~in_1[4], in_1[5]);  // AND_Gate
  and and_5 (out_12, OL100, OH000);
  and and_6 (out_13, OL101, OH000);
  and and_7 (out_14, OL110, OH000);
  and and_8 (out_15, OL111, OH000);
  and and_9 (out_16, OL001, OH000);
  or or_1 (out_11, out_10, read0);
  or or_2 (read0, out_12, out_13, out_14, out_15, out_16);
  and and_10 (OL001, in_1[0], ~in_1[1], ~in_1[2]);  // AND_Gate
  and and_11 (OH001, in_1[3], ~in_1[4], ~in_1[5]);  // AND_Gate
  and and_12 (OL101, in_1[0], ~in_1[1], in_1[2]);  // AND_Gate
  and and_13 (OH101, in_1[3], ~in_1[4], in_1[5]);  // AND_Gate
  and and_14 (out_5, OL100, OH001);
  and and_15 (out_7, OL101, OH001);
  and and_16 (out_8, OL110, OH001);
  and and_17 (out_3, OL010, OH001);
  and and_18 (out_4, OL011, OH001);
  and and_19 (and_19_out, OL000, OH001);
  and and_20 (OL010, ~in_1[0], in_1[1], ~in_1[2]);  // AND_Gate
  and and_21 (OL110, ~in_1[0], in_1[1], in_1[2]);  // AND_Gate
  or or_3 (out_2, and_19_out, addi0);
  or or_4 (out_6, out_5, out_7, out_8, out_3, out_4, out_2);
  and and_22 (OL011, in_1[0], in_1[1], ~in_1[2]);  // AND_Gate
  and and_23 (OL111, in_1[0], in_1[1], in_1[2]);
  or or_5 (addi0, out_9, out_10);
  and and_24 (out_9, OH100, OL011);
  and and_25 (out_10, OH101, OL011);

  // Other names for the same wires on the sheet: addi = out_2; andi = out_5; beq = out_12; bgtz = out_15;
  //   blez = out_14; bltz = out_16; bne = out_13; inmediate = out_6; lw = out_9; Op_Code[5:0] = in_1; ori = out_7;
  //   read = out_11; slti = out_3; sltiu = out_4; sw = out_10; xori = out_8

  // Notes on the sheet:
  //   Op Lectura
  //   Etiquetas TipoI
endmodule

module Branch_Control (
  input  in_1,
  input  [15:0] in_2,
  input  in_3,
  input  [31:0] in_4,
  input  [31:0] in_5,
  input  in_6,
  input  [25:0] in_7,
  input  in_8,
  input  in_9,
  input  [31:0] in_10,
  input  in_11,
  input  in_12,
  output [31:0] out_13
);

  wire and_1_out, and_2_out, and_3_out, and_4_out, and_5_out, comparator_2_eq, or_2_out, Rs_0, Rs_0_t, Rs__0,
       Rs__Rt, Rs__Rt_t;
  wire [1:0] selector;
  wire [31:0] bit_extender_1_out, PC_4, PC_4_4_offset;

  Comparator #(.width(32)) comparator_1 (.a(in_10), .b(in_5), .eq(Rs__Rt_t));  // open: gt, lt
  Comparator #(.width(32)) comparator_2 (.a(in_10), .b({32{1'b0}}), .gt(Rs_0_t), .eq(comparator_2_eq), .lt(Rs_0));
  not not_1 (Rs__Rt, Rs__Rt_t);
  or or_1 (Rs__0, comparator_2_eq, Rs_0);
  Multiplexer #(.select(2), .width(32), .enable("false")) multiplexer_1 (
    .in0(PC_4), .in1(PC_4_4_offset), .in2({in_4[31:28], in_7, 2'b00}), .in3(in_10), .out(out_13),
    .sel(selector));
  and and_1 (and_1_out, Rs__Rt_t, in_9);
  and and_2 (and_2_out, Rs__Rt, in_8);
  and and_3 (and_3_out, Rs__0, in_6);
  and and_4 (and_4_out, Rs_0_t, in_3);
  and and_5 (and_5_out, Rs_0, in_1);
  or or_2 (or_2_out, and_1_out, and_2_out, and_3_out, and_4_out, and_5_out);
  or or_3 (selector[1], in_11, in_12);
  or or_4 (selector[0], or_2_out, in_12);
  Adder #(.width(32)) adder_1 (.a(in_4), .b(32'h4), .out(PC_4));  // open: cin, cout
  assign bit_extender_1_out = {{14{in_2[15]}}, {in_2, 2'b00}};  // Bit_Extender bit_extender_1
  Adder #(.width(32)) adder_2 (.a(PC_4), .b(bit_extender_1_out), .out(PC_4_4_offset));  // open: cin, cout

  // Other names for the same wires on the sheet: Constante[15:0] = in_2; beq = in_9; bgtz = in_3; blez = in_6;
  //   bltz = in_1; bne = in_8; IA_prime[31:0] = out_13; j = in_11; jr = in_12; Destino[25:0] = in_7;
  //   Jump[31:2] = {in_4[31:28], in_7}; PC[31:0] = in_4; Rs[31:0] = in_10; Rt[31:0] = in_5

  // Notes on the sheet:
  //   Condiciones
  //   Proxima instruccion
  //   Selector
  //   Etiquetas
endmodule

module Program_Counter (
  input  in_1,
  input  in_2,
  input  in_3,
  input  [31:0] in_4,
  output [31:0] Output
);

  Register #(.width(32)) register_1 (.D(in_4), .en(in_3), .Q(Output), .clk(in_1), .clr(in_2));

  // Other names for the same wires on the sheet: clk = in_1; enable = in_3; reset = in_2
endmodule

module RAM_Interaction (
  input  in_1,
  input  [31:0] in_2,
  input  [31:0] in_3,
  input  in_4,
  input  in_5,
  input  in_6,
  input  in_7,
  input  [31:0] in_8,
  input  [31:0] in_9,
  input  in_10,
  input  [3:0] in_11,
  input  [31:0] in_12,
  input  [3:0] in_13,
  output [31:0] out_14,
  output [31:0] out_15,
  output [31:0] out_16,
  output [31:0] out_17,
  output [15:0] out_18,
  output out_19,
  output out_20,
  output [3:0] out_21,
  output out_22,
  output out_23,
  output out_24
);

  wire CSD, CSR, or_2_out, Stop;
  wire [31:0] DO0, DO1, DO2, DO3, Out0, Out1, Out2, Out3, switch_1_output, switch_2_output, switch_3_output,
       switch_4_output;

  RAM_Reader ram_reader_1 (
    .in_1(in_2), .in_3(in_8), .in_2(in_3), .in_4(in_9), .in_5(in_11), .in_6(in_1), .in_7(in_4), .in_8(in_6),
    .out_9(Out0), .out_11(Out1), .out_10(Out2), .out_12(Out3), .out_13(CSR), .out_14(out_19));
  Demultiplexer #(.select(2)) demultiplexer_1 (
    .out0(out_21[0]), .out1(out_21[1]), .out2(out_21[2]), .out3(out_21[3]), .in(1'b1), .sel(in_12[3:2]));  // open: en
  or or_1 (out_24, CSR, out_23, CSD);
  D_Flip_Flop #(.trigger("falling")) d_ff_1 (
    .clk(in_1), .D(in_5), .Q(out_23), .en(or_2_out));  // open: Qn, preset, reset
  or or_2 (or_2_out, in_5, Stop);
  Switch switch_1 (.Input(DO0), .Output(switch_1_output));
  Switch switch_2 (.Input(DO2), .Output(switch_2_output));
  Multiplexer #(.width(32), .enable("false")) multiplexer_1 (
    .in0(switch_1_output), .in1(Out0), .out(out_14), .sel(in_10));
  Multiplexer #(.width(32), .enable("false")) multiplexer_2 (
    .in0(switch_2_output), .in1(Out2), .out(out_15), .sel(in_10));
  RAM_Reader ram_reader_2 (
    .in_1(in_2), .in_3(in_8), .in_2(in_3), .in_4(in_9), .in_5(in_11), .in_6(in_1), .in_7(in_4), .in_8(in_7),
    .out_9(DO0), .out_11(DO1), .out_10(DO2), .out_12(DO3), .out_13(CSD), .out_14(out_20));
  Timer timer_1 (.in_1(out_23), .Ready(Stop), .in_2(out_22), .in_3(in_1), .in_4(in_13));
  D_Flip_Flop #(.trigger("falling")) d_ff_2 (.clk(in_1), .D(Stop), .Q(out_22));  // open: Qn, preset, en, reset
  Switch switch_3 (.Input(DO1), .Output(switch_3_output));
  Switch switch_4 (.Input(DO3), .Output(switch_4_output));
  Multiplexer #(.width(32), .enable("false")) multiplexer_3 (
    .in0(switch_3_output), .in1(Out1), .out(out_16), .sel(in_10));
  Multiplexer #(.width(32), .enable("false")) multiplexer_4 (
    .in0(switch_4_output), .in1(Out3), .out(out_17), .sel(in_10));

  assign out_18 = in_12[19:4];

  // Other names for the same wires on the sheet: Bank0[31:0] = in_2; Bank1[31:0] = in_8; Bank2[31:0] = in_3;
  //   Bank3[31:0] = in_9; BankOut0[31:0] = out_14; BankOut1[31:0] = out_16; BankOut2[31:0] = out_15;
  //   BankOut3[31:0] = out_17; Clk = in_1; CS = out_24; DPAddress[31:0] = in_12; AddressRAM[15:0] = in_12[19:4];
  //   getData = in_7; getInst = in_6; isInst = in_10; Mask[3:0] = out_21; ReadTime[3:0] = in_11; ReadyData = out_20;
  //   ReadyInst = out_19; ReadyWrite = out_22; reset = in_4; RW = out_23; Write = in_5; WriteTime[3:0] = in_13

  // Notes on the sheet:
  //   Chip Select
  //   Mask - AddressRAM
  //   RAM_Readers
  //   Entradas
  //   ReadyWrite
  //   Select BankOut
  //   Salidas
endmodule

module RAM_Reader (
  input  [31:0] in_1,
  input  [31:0] in_2,
  input  [31:0] in_3,
  input  [31:0] in_4,
  input  [3:0] in_5,
  input  in_6,
  input  in_7,
  input  in_8,
  output [31:0] out_9,
  output [31:0] out_10,
  output [31:0] out_11,
  output [31:0] out_12,
  output out_13,
  output out_14
);

  wire CS0, enReg, or_1_out, Stop;

  D_Flip_Flop #(.trigger("falling")) d_ff_1 (.clk(in_6), .D(in_8), .Q(CS0), .en(or_1_out));  // open: Qn, preset, reset
  or or_1 (or_1_out, in_8, Stop);
  or or_2 (out_13, CS0, enReg);
  Timer timer_1 (.in_1(CS0), .Ready(Stop), .in_2(out_14), .in_3(in_6), .in_4(in_5));
  D_Flip_Flop #(.trigger("falling")) d_ff_2 (.clk(in_6), .D(Stop), .Q(enReg), .reset(out_14));  // open: Qn, preset, en
  D_Flip_Flop #(.trigger("falling")) d_ff_3 (.clk(in_6), .D(enReg), .Q(out_14));  // open: Qn, preset, en, reset
  Register #(.width(32)) register_1 (.D(in_1), .en(enReg), .Q(out_9), .clk(in_6), .clr(in_7));
  Register #(.width(32)) register_2 (.D(in_3), .en(enReg), .Q(out_11), .clk(in_6), .clr(in_7));
  Register #(.width(32)) register_3 (.D(in_4), .en(enReg), .Q(out_12), .clk(in_6), .clr(in_7));
  Register #(.width(32)) register_4 (.D(in_2), .en(enReg), .Q(out_10), .clk(in_6), .clr(in_7));

  // Other names for the same wires on the sheet: Bank0[31:0] = in_1; Bank1[31:0] = in_3; Bank2[31:0] = in_2;
  //   Bank3[31:0] = in_4; BankOut0[31:0] = out_9; BankOut1[31:0] = out_11; BankOut2[31:0] = out_10;
  //   BankOut3[31:0] = out_12; clk = in_6; CS = out_13; get = in_8; ReadTime[3:0] = in_5; ready = out_14;
  //   reset = in_7

  // Notes on the sheet:
  //   Chip Select
  //   Entradas
  //   Ready Read
  //   Salidas
  //   Registros Bank
endmodule

module Timer (
  input  in_1,
  input  in_2,
  input  in_3,
  input  [3:0] in_4,
  output Ready
);

  wire [3:0] counter_1_q;

  Counter #(.width(4), .max('hf)) counter_1 (
    .count(in_1), .Q(counter_1_q), .clk(in_3), .clr(in_2));  // open: load, D, carry
  Comparator #(.width(4)) comparator_1 (.a(in_4), .b(counter_1_q), .eq(Ready));  // open: gt, lt

  // Other names for the same wires on the sheet: Clk = in_3; Reset = in_2; Start = in_1; Time[3:0] = in_4

  // Notes on the sheet:
  //   Entradas
  //   Salida
endmodule

module Switch (
  input  [31:0] Input,
  output [31:0] Output
);


  assign Output = {Input[7:0], Input[15:8], Input[23:16], Input[31:24]};
endmodule

module Get_Instruction (
  input  in_1,
  input  [31:0] in_2,
  input  in_3,
  input  in_4,
  output [31:0] out_5
);

  Register #(.width(32)) register_1 (
    .D(in_2), .en(in_4), .Q({out_5[7:0], out_5[15:8], out_5[23:16], out_5[31:24]}), .clk(in_1), .clr(in_3));

  // Other names for the same wires on the sheet: clk = in_1; enable = in_4; inst[31:0] = in_2; out[31:0] = out_5;
  //   reset = in_3
endmodule

module MemoryAddress (
  input  [31:0] in_1,
  input  in_2,
  input  in_3,
  input  in_4,
  input  [31:0] in_5,
  input  in_6,
  input  in_7,
  input  [31:0] in_8,
  output [31:0] Output
);

  wire [1:0] or_1_out;
  wire [31:0] multiplexer_1_out, subtractor_1_out;

  Subtractor #(.width(32)) subtractor_1 (.a(in_8), .b(32'h4), .out(subtractor_1_out));  // open: bin, bout
  Multiplexer #(.width(32), .enable("false")) multiplexer_1 (
    .in0(in_8), .in1(subtractor_1_out), .out(multiplexer_1_out), .sel(in_3));
  Multiplexer #(.select(2), .width(32), .enable("false")) multiplexer_2 (
    .in0(in_5), .in1(in_1), .in2(multiplexer_1_out), .in3(in_5), .out(Output), .sel(or_1_out));
  or or_1 (or_1_out[0], in_4, in_7, in_6);
  or or_2 (or_1_out[1], in_3, in_7, in_2);

  // Other names for the same wires on the sheet: ALU[31:0] = in_1; enablePC = in_7; lw = in_4; PC[31:0] = in_5;
  //   pop = in_2; push = in_3; SP[31:0] = in_8; sw = in_6

  // Notes on the sheet:
  //   Entradas
  //   Salida
endmodule

module Control_Unit (
  input  in_1,
  input  in_2,
  input  in_3,
  input  in_4,
  input  in_5,
  input  in_6,
  input  in_7,
  input  in_8,
  input  in_9,
  input  in_10,
  input  in_11,
  input  in_12,
  output out_13,
  output out_14,
  output out_15,
  output out_16,
  output out_17,
  output out_18,
  output out_19,
  output out_20,
  output out_21
);

  wire Branch, d_ff_1_q, d_ff_2_q, d_ff_3_q, d_ff_5_q, demultiplexer_1_out0, demultiplexer_1_out1, or_5_out,
       RF;
  wire [2:0] or_1_out;

  D_Flip_Flop #(.trigger("falling")) d_ff_1 (.clk(in_1), .D(in_2), .Q(d_ff_1_q), .reset(in_6));  // open: Qn, preset, en
  or or_1 (or_1_out[0], in_5, in_4, in_11);
  or or_2 (or_1_out[1], in_5, in_9);
  or or_3 (or_1_out[2], in_10, in_11);
  D_Flip_Flop #(.trigger("falling")) d_ff_2 (
    .clk(in_1), .D(out_14), .Q(d_ff_2_q), .reset(in_6));  // open: Qn, preset, en
  D_Flip_Flop #(.trigger("falling")) d_ff_3 (.clk(in_1), .D(in_3), .Q(d_ff_3_q));  // open: Qn, preset, en, reset
  Demultiplexer #(.select(3)) demultiplexer_1 (
    .out0(demultiplexer_1_out0), .out1(demultiplexer_1_out1), .out2(Branch), .out3(RF), .out4(out_16),
    .out5(out_21), .in(d_ff_3_q), .sel(or_1_out));  // open: out6, out7, en
  or or_4 (out_17, d_ff_1_q, d_ff_2_q);
  or or_5 (or_5_out, out_15, demultiplexer_1_out0);
  D_Flip_Flop #(.trigger("falling")) d_ff_4 (
    .clk(in_1), .D(or_5_out), .Q(out_15), .reset(in_6));  // open: Qn, preset, en
  D_Flip_Flop #(.trigger("falling")) d_ff_5 (
    .clk(in_1), .D(demultiplexer_1_out1), .Q(d_ff_5_q), .reset(in_6));  // open: Qn, preset, en
  or or_6 (out_13, d_ff_5_q, in_8, RF);
  and and_1 (out_19, out_20, in_7);
  D_Flip_Flop #(.trigger("falling")) d_ff_6 (.clk(in_1), .D(out_13), .Q(out_20));  // open: Qn, preset, en, reset
  or or_7 (out_14, out_20, in_12, Branch);

  assign out_18 = in_3;

  // Other names for the same wires on the sheet: AluInst = in_4; Clk = in_1; End = out_15; getData = out_16;
  //   getInst = out_17; JmpInst = in_9; MemInst = in_10; ReadyData = in_8; ReadyW = in_12; Reset = in_6; RInst = in_5;
  //   Start = in_2; KbdEn = out_20; Tty = out_20; TtyEn = out_19; TtyInst = in_7; ReadyInst = in_3; useGI = in_3;
  //   Cont = out_14; usePC = out_14; useRF = out_13; Write = out_21; WriteInst = in_11
endmodule
